// Logisim project RAIYAN MASOOD HRIDDHO-1931117042-CSE-332 LAB-SECTION NO-01-ASSIGNMENT NO-03-SUMMER-2023 SEMESTER.circ as structural Verilog: 2 circuits, main circuit main
module main (
  input  [31:0] WriteData,
  input  CLK,
  input  Write,
  input  [4:0] WriteReg,
  input  [4:0] Read1,
  input  [4:0] Read2,
  output [31:0] ReadReg1,
  output [31:0] ReadReg2
);

  wire [7:0] decoder_1_out0, decoder_1_out8, decoder_1_out16, decoder_1_out24;
  wire [31:0] register_1_q, register_2_q, register_3_q, register_4_q, register_5_q, register_6_q,
       register_7_q, register_8_q, register_9_q, register_10_q, register_11_q, register_12_q, register_13_q,
       register_14_q, register_15_q, register_16_q, register_17_q, register_18_q, register_19_q,
       register_20_q, register_21_q, register_22_q, register_23_q, register_24_q, register_25_q,
       register_26_q, register_27_q, register_28_q, register_29_q, register_30_q, register_31_q,
       register_32_q;

  Decoder #(.select(5)) decoder_1 (
    .out0(decoder_1_out0[0]), .out1(decoder_1_out0[1]), .out2(decoder_1_out0[2]), .out3(decoder_1_out0[3]),
    .out4(decoder_1_out0[4]), .out5(decoder_1_out0[5]), .out6(decoder_1_out0[6]), .out7(decoder_1_out0[7]),
    .out8(decoder_1_out8[0]), .out9(decoder_1_out8[1]), .out10(decoder_1_out8[2]), .out11(decoder_1_out8[3]),
    .out12(decoder_1_out8[4]), .out13(decoder_1_out8[5]), .out14(decoder_1_out8[6]),
    .out15(decoder_1_out8[7]), .out16(decoder_1_out16[0]), .out17(decoder_1_out16[1]),
    .out18(decoder_1_out16[2]), .out19(decoder_1_out16[3]), .out20(decoder_1_out16[4]),
    .out21(decoder_1_out16[5]), .out22(decoder_1_out16[6]), .out23(decoder_1_out16[7]),
    .out24(decoder_1_out24[0]), .out25(decoder_1_out24[1]), .out26(decoder_1_out24[2]),
    .out27(decoder_1_out24[3]), .out28(decoder_1_out24[4]), .out29(decoder_1_out24[5]),
    .out30(decoder_1_out24[6]), .out31(decoder_1_out24[7]), .sel(WriteReg), .en(Write));
  Register #(.width(32)) register_1 (.D(WriteData), .en(decoder_1_out0[0]), .clk(CLK), .Q(register_1_q));  // open: clr
  Register #(.width(32)) register_2 (.D(WriteData), .en(decoder_1_out8[0]), .clk(CLK), .Q(register_2_q));  // open: clr
  Register #(.width(32)) register_3 (.D(WriteData), .en(decoder_1_out16[0]), .clk(CLK), .Q(register_3_q));  // open: clr
  Register #(.width(32)) register_4 (.D(WriteData), .en(decoder_1_out24[0]), .clk(CLK), .Q(register_4_q));  // open: clr
  Register #(.width(32)) register_5 (.D(WriteData), .en(decoder_1_out0[1]), .clk(CLK), .Q(register_5_q));  // open: clr
  Register #(.width(32)) register_6 (.D(WriteData), .en(decoder_1_out8[1]), .clk(CLK), .Q(register_6_q));  // open: clr
  Register #(.width(32)) register_7 (.D(WriteData), .en(decoder_1_out16[1]), .clk(CLK), .Q(register_7_q));  // open: clr
  Register #(.width(32)) register_8 (.D(WriteData), .en(decoder_1_out24[1]), .clk(CLK), .Q(register_8_q));  // open: clr
  Register #(.width(32)) register_9 (.D(WriteData), .en(decoder_1_out0[2]), .Q(register_9_q));  // open: clk, clr
  Register #(.width(32)) register_10 (
    .D(WriteData), .en(decoder_1_out8[2]), .clk(CLK), .Q(register_10_q));  // open: clr
  Register #(.width(32)) register_11 (
    .D(WriteData), .en(decoder_1_out16[2]), .clk(CLK), .Q(register_11_q));  // open: clr
  Register #(.width(32)) register_12 (
    .D(WriteData), .en(decoder_1_out24[2]), .clk(CLK), .Q(register_12_q));  // open: clr
  Register #(.width(32)) register_13 (
    .D(WriteData), .en(decoder_1_out0[3]), .clk(CLK), .Q(register_13_q));  // open: clr
  Register #(.width(32)) register_14 (
    .D(WriteData), .en(decoder_1_out8[3]), .clk(CLK), .Q(register_14_q));  // open: clr
  Register #(.width(32)) register_15 (
    .D(WriteData), .en(decoder_1_out16[3]), .clk(CLK), .Q(register_15_q));  // open: clr
  Register #(.width(32)) register_16 (
    .D(WriteData), .en(decoder_1_out24[3]), .clk(CLK), .Q(register_16_q));  // open: clr
  Register #(.width(32)) register_17 (
    .D(WriteData), .en(decoder_1_out0[4]), .clk(CLK), .Q(register_17_q));  // open: clr
  Register #(.width(32)) register_18 (
    .D(WriteData), .en(decoder_1_out8[4]), .clk(CLK), .Q(register_18_q));  // open: clr
  Register #(.width(32)) register_19 (
    .D(WriteData), .en(decoder_1_out16[4]), .clk(CLK), .Q(register_19_q));  // open: clr
  Register #(.width(32)) register_20 (
    .D(WriteData), .en(decoder_1_out24[4]), .clk(CLK), .Q(register_20_q));  // open: clr
  Register #(.width(32)) register_21 (
    .D(WriteData), .en(decoder_1_out0[5]), .clk(CLK), .Q(register_21_q));  // open: clr
  Register #(.width(32)) register_22 (
    .D(WriteData), .en(decoder_1_out8[5]), .clk(CLK), .Q(register_22_q));  // open: clr
  Register #(.width(32)) register_23 (
    .D(WriteData), .en(decoder_1_out16[5]), .clk(CLK), .Q(register_23_q));  // open: clr
  Register #(.width(32)) register_24 (
    .D(WriteData), .en(decoder_1_out24[5]), .clk(CLK), .Q(register_24_q));  // open: clr
  Register #(.width(32)) register_25 (
    .D(WriteData), .en(decoder_1_out0[6]), .clk(CLK), .Q(register_25_q));  // open: clr
  Register #(.width(32)) register_26 (
    .D(WriteData), .en(decoder_1_out8[6]), .clk(CLK), .Q(register_26_q));  // open: clr
  Register #(.width(32)) register_27 (
    .D(WriteData), .en(decoder_1_out16[6]), .clk(CLK), .Q(register_27_q));  // open: clr
  Register #(.width(32)) register_28 (
    .D(WriteData), .en(decoder_1_out24[6]), .clk(CLK), .Q(register_28_q));  // open: clr
  Register #(.width(32)) register_29 (
    .D(WriteData), .en(decoder_1_out0[7]), .clk(CLK), .Q(register_29_q));  // open: clr
  Register #(.width(32)) register_30 (
    .D(WriteData), .en(decoder_1_out8[7]), .clk(CLK), .Q(register_30_q));  // open: clr
  Register #(.width(32)) register_31 (
    .D(WriteData), .en(decoder_1_out16[7]), .clk(CLK), .Q(register_31_q));  // open: clr
  Register #(.width(32)) register_32 (
    .D(WriteData), .en(decoder_1_out24[7]), .clk(CLK), .Q(register_32_q));  // open: clr
  Multiplexer #(.select(5), .width(32)) multiplexer_1 (
    .in0(register_1_q), .in1(register_5_q), .in2(register_9_q), .in3(register_13_q), .in4(register_17_q),
    .in5(register_21_q), .in6(register_25_q), .in7(register_29_q), .in8(register_2_q), .in9(register_6_q),
    .in10(register_10_q), .in11(register_14_q), .in12(register_18_q), .in13(register_22_q),
    .in14(register_26_q), .in15(register_30_q), .in16(register_3_q), .in17(register_7_q),
    .in18(register_11_q), .in19(register_15_q), .in20(register_19_q), .in21(register_23_q),
    .in22(register_27_q), .in23(register_31_q), .in24(register_4_q), .in25(register_8_q),
    .in26(register_12_q), .in27(register_16_q), .in28(register_20_q), .in29(register_24_q),
    .in30(register_28_q), .in31(register_32_q), .out(ReadReg1), .sel(Read1));
  Multiplexer #(.select(5), .width(32)) multiplexer_2 (
    .in0(register_1_q), .in1(register_5_q), .in2(register_9_q), .in3(register_13_q), .in4(register_17_q),
    .in5(register_21_q), .in6(register_25_q), .in7(register_29_q), .in8(register_2_q), .in9(register_6_q),
    .in10(register_10_q), .in11(register_14_q), .in12(register_18_q), .in13(register_22_q),
    .in14(register_26_q), .in15(register_30_q), .in16(register_3_q), .in17(register_7_q),
    .in18(register_11_q), .in19(register_15_q), .in20(register_19_q), .in21(register_23_q),
    .in22(register_27_q), .in23(register_31_q), .in24(register_4_q), .in25(register_8_q),
    .in26(register_12_q), .in27(register_16_q), .in28(register_20_q), .in29(register_24_q),
    .in30(register_28_q), .in31(register_32_q), .out(ReadReg2), .sel(Read2));
endmodule

module IC (
  input  [31:0] in_1,
  input  in_2,
  input  in_3,
  input  [4:0] in_4,
  input  [4:0] in_5,
  input  [4:0] in_6,
  output [31:0] out_7,
  output [31:0] out_8
);

  main main_1 (
    .WriteData(in_1), .CLK(in_2), .Write(in_3), .WriteReg(in_4), .Read1(in_5), .Read2(in_6),
    .ReadReg1(out_7), .ReadReg2(out_8));
endmodule
